// Digital circuit 32_Comptur.dig as structural Verilog
module _32_Comptur (
  input  [31:0] in_1,
  input  clk,
  input  [4:0] in_3,
  input  in_4,
  input  [4:0] in_5,
  input  [4:0] in_7,
  input  [1:0] in_9,
  input  [15:0] in_10,
  input  in_11,
  input  in_12,
  input  in_13,
  input  in_14,
  input  in_15,
  input  in_16,
  output out_6,
  output [31:0] out_8,
  output [31:0] out_17,
  output [31:0] out_18
);

  wire pullup_1_out, pullup_2_out;
  wire [4:0] multiplexer_1_out;
  wire [31:0] BusA, BusB, BusW, Ext_OUT, Mem_OUT, multiplexer_2_out;

  PC pc_1 (.OUT(out_17), .imm16(out_18[15:0]), .nPC_sel(in_16), .CLK(clk), .En(pullup_1_out));
  PullUp pullup_1 (.out(pullup_1_out));
  PullUp pullup_2 (.out(pullup_2_out));
  Multiplexer #(.Bits(5)) multiplexer_1 (
    .sel(in_15), .in_0(out_18[25:21]), .in_1(out_18[15:11]), .out(multiplexer_1_out));
  ROM #(.AddrBits(24), .Bits(32)) rom_1 (.A(out_17[23:0]), .sel(pullup_2_out), .D(out_18));
  // Extender extender_1: pin names not known; wires that end beside it: out_18[15:0], in_12, Ext_OUT
  RegisterFile #(.AddrBits(5), .Bits(32)) registerfile_1 (
    .Din(BusW), .we(in_4), .Rw(multiplexer_1_out), .C(clk), .Ra(out_18[20:16]), .Rb(out_18[25:21]),
    .Da(BusA), .Db(BusB));
  Multiplexer #(.Bits(32)) multiplexer_2 (.sel(in_11), .in_0(BusB), .in_1(Ext_OUT), .out(multiplexer_2_out));
  ALU alu_1 (.ALU_CTR(in_9), .A(BusA), .B(multiplexer_2_out), .OUT(out_8), .ZERO(out_6));
  BlockRAMDualPort #(.AddrBits(5), .Bits(32)) Date_Memory (
    .A(out_8[4:0]), .Din(BusB), .str(in_13), .C(clk), .D(Mem_OUT));
  Multiplexer #(.Bits(32)) multiplexer_3 (.sel(in_14), .in_0(out_8), .in_1(Mem_OUT), .out(BusW));

  // Other names for the same wires on the sheet: ALU_OUT[31:0] = out_8; ALUctr[1:0] = in_9; ALUSrc = in_11;
  //   ExtOp = in_12; MemtoReg = in_14; MemWr = in_13; nPC_sel = in_16; Func[5:0] = out_18[5:0];
  //   imm16[15:0] = out_18[15:0]; Shamt[4:0] = out_18[10:6]; Rd[4:0] = out_18[15:11]; Rs[4:0] = out_18[20:16];
  //   Rt[4:0] = out_18[25:21]; OP[5:0] = out_18[31:26]; PC_Counter[31:0] = out_17; RegDst = in_15; RegWr = in_4;
  //   Zero = out_6

  // Notes on the sheet:
  //   contents of rom_1 (hex, n*v repeats v):
  //   ffffffff,0,0,0,bbbbbbbb,0,0,0,ffffffff,0,0,0,bbbbbbbb,0,0,0,ffffffff
  //   ,0,0,0,bbbbbbbb,0,0,0,ffffffff,0,0,0,bbbbbbbb,0,0,0,ffffffff,0,0,0
  //   ,bbbbbbbb,0,0,0,ffffffff,0,0,0,bbbbbbbb,0,0,0,ffffffff,0,0,0,bbbbbbbb
  //   ,0,0,0,ffffffff,0,0,0,bbbbbbbb,0,0,0,ffffffff,0,0,0,bbbbbbbb,0,0,0
  //   ,ffffffff,0,0,0,bbbbbbbb,0,0,0,ffffffff,0,0,0,bbbbbbbb,0,0,0,ffffffff
  //   ,0,0,0,bbbbbbbb,0,0,0,ffffffff,0,0,0,bbbbbbbb,0,0,0,ffffffff,0,0,0
  //   ,bbbbbbbb,0,0,0,ffffffff,0,0,0,bbbbbbbb
  //   32-bit
  //   Registers
endmodule
