// Digital circuit 32_Computer.dig as structural Verilog
module _32_Computer (
  input  [31:0] in_1,
  input  [4:0] in_2,
  input  in_3,
  input  [4:0] in_4,
  input  [4:0] in_6,
  input  [2:0] in_8,
  input  [15:0] in_9,
  input  in_10,
  input  in_11,
  input  in_12,
  input  in_13,
  input  in_14,
  input  in_15,
  input  clk,
  input  in_19,
  input  [2:0] in_20,
  input  in_21,
  input  clk_2,
  output out_5,
  output [31:0] out_7,
  output [31:0] out_16,
  output [31:0] out_17
);

  wire ALU_Src, Branch, Ext_Op, Jal_ctr, Mem_Re, Mem_Wr, MemtoReg, pullup_1_out, Reg_Dst, Reg_Wr;
  wire [2:0] ALU_ctr, ALU_Op;
  wire [4:0] multiplexer_1_out, Rd, Rs, Rt, Shamt;
  wire [5:0] Func, OP;
  wire [15:0] imm16;
  wire [31:0] Bus_A, Bus_B, Bus_W, Ext_OUT, Mem_OUT, multiplexer_2_out;

  Control control_1 (
    .OP_CODE(OP), .RegDst(Reg_Dst), .ALUSrc(ALU_Src), .MemToReg(MemtoReg), .RegWrite(Reg_Wr),
    .MemRead(Mem_Re), .MemWrite(Mem_Wr), .Branch(Branch), .ALUOp(ALU_Op), .JaLCtr(Jal_ctr), .ExtOp(Ext_Op));
  instruction_memory instruction_memory_1 (
    .A(out_16[23:0]), .CLK(clk), .D(out_17), .OP(OP), .Rs(Rs), .Rt(Rt), .Rd(Rd), .Shamt(Shamt), .Func(Func),
    .imm16(imm16));
  PC pc_1 (
    .OUT(out_16), .imm16(imm16), .Branch(Branch), .Zero(out_5), .Jal_ctr(Jal_ctr), .CLK(clk_2),
    .En(pullup_1_out));
  PullUp pullup_1 (.out(pullup_1_out));
  Seven_Seg_Hex seven_seg_hex_1 (.d(Bus_A[31:28]), .dp(1'b0));
  Seven_Seg_Hex seven_seg_hex_2 (.d(Bus_B[31:28]), .dp(1'b0));
  Seven_Seg_Hex seven_seg_hex_3 (.d(out_7[31:28]), .dp(1'b0));
  Seven_Seg_Hex seven_seg_hex_4 (.d(Bus_A[27:24]), .dp(1'b0));
  Seven_Seg_Hex seven_seg_hex_5 (.d(Bus_B[27:24]), .dp(1'b0));
  Seven_Seg_Hex seven_seg_hex_6 (.d(out_7[27:24]), .dp(1'b0));
  Seven_Seg_Hex seven_seg_hex_7 (.d(Bus_A[23:20]), .dp(1'b0));
  Seven_Seg_Hex seven_seg_hex_8 (.d(Bus_B[23:20]), .dp(1'b0));
  Seven_Seg_Hex seven_seg_hex_9 (.d(out_7[23:20]), .dp(1'b0));
  Seven_Seg_Hex seven_seg_hex_10 (.d(Bus_A[19:16]), .dp(1'b0));
  Seven_Seg_Hex seven_seg_hex_11 (.d(Bus_B[19:16]), .dp(1'b0));
  Seven_Seg_Hex seven_seg_hex_12 (.d(out_7[19:16]), .dp(1'b0));
  Seven_Seg_Hex seven_seg_hex_13 (.d(Bus_A[15:12]), .dp(1'b0));
  Seven_Seg_Hex seven_seg_hex_14 (.d(Bus_B[15:12]), .dp(1'b0));
  Seven_Seg_Hex seven_seg_hex_15 (.d(out_7[15:12]), .dp(1'b0));
  Multiplexer #(.Bits(5)) multiplexer_1 (.sel(Reg_Dst), .in_0(Rt), .in_1(Rd), .out(multiplexer_1_out));
  Seven_Seg_Hex seven_seg_hex_16 (.d(Bus_A[11:8]), .dp(1'b0));
  Seven_Seg_Hex seven_seg_hex_17 (.d(Bus_B[11:8]), .dp(1'b0));
  Seven_Seg_Hex seven_seg_hex_18 (.d(out_7[11:8]), .dp(1'b0));
  Seven_Seg_Hex seven_seg_hex_19 (.d(Bus_A[7:4]), .dp(1'b0));
  Seven_Seg_Hex seven_seg_hex_20 (.d(Bus_B[7:4]), .dp(1'b0));
  Seven_Seg_Hex seven_seg_hex_21 (.d(out_7[7:4]), .dp(1'b0));
  // Extender extender_1: pin names not known; wires that end beside it: imm16, Ext_Op, Ext_OUT
  Seven_Seg_Hex seven_seg_hex_22 (.d(Bus_A[3:0]), .dp(1'b0));
  Seven_Seg_Hex seven_seg_hex_23 (.d(Bus_B[3:0]), .dp(1'b0));
  Seven_Seg_Hex seven_seg_hex_24 (.d(out_7[3:0]), .dp(1'b0));
  RegisterFile #(.AddrBits(5), .Bits(32)) registerfile_1 (
    .Din(Bus_W), .we(Reg_Wr), .Rw(multiplexer_1_out), .C(clk_2), .Ra(Rs), .Rb(Rt), .Da(Bus_A), .Db(Bus_B));
  ALU_Controll alu_controll_1 (.ALU_Op(ALU_Op), .func(Func), .ALU_CTR(ALU_ctr));  // open: J_CTR
  Multiplexer #(.Bits(32)) multiplexer_2 (.sel(ALU_Src), .in_0(Bus_B), .in_1(Ext_OUT), .out(multiplexer_2_out));
  ALU alu_1 (.ALU_CTR(ALU_ctr), .A(Bus_A), .B(multiplexer_2_out), .OUT(out_7), .ZERO(out_5));
  RAMDualPort #(.AddrBits(5), .Bits(32)) Data_Memory (
    .A(out_7[4:0]), .Din(Bus_B), .str(Mem_Wr), .C(clk_2), .ld(Mem_Re), .D(Mem_OUT));
  Multiplexer #(.Bits(32)) multiplexer_3 (.sel(MemtoReg), .in_0(out_7), .in_1(Mem_OUT), .out(Bus_W));
  Seven_Seg_Hex seven_seg_hex_25 (.d(Bus_A[7:4]), .dp(1'b0));
  Seven_Seg_Hex seven_seg_hex_26 (.d(Bus_B[7:4]), .dp(1'b0));
  Seven_Seg_Hex seven_seg_hex_27 (.d(out_7[7:4]), .dp(1'b0));
  Seven_Seg_Hex seven_seg_hex_28 (.d(Bus_A[3:0]), .dp(1'b0));
  Seven_Seg_Hex seven_seg_hex_29 (.d(Bus_B[3:0]), .dp(1'b0));
  Seven_Seg_Hex seven_seg_hex_30 (.d(out_7[3:0]), .dp(1'b0));

  // Other names for the same wires on the sheet: ALU_OUT[31:0] = out_7; CLK_t = clk_2; PC_Counter[31:0] = out_16;
  //   Zero = out_5

  // Notes on the sheet:
  //   clk: Hz: 2147483647
  //   32-bit
  //   Registers
endmodule
