// Digital circuit ALU.dig as structural Verilog
module ALU (
  input  [2:0] ALU_CTR,
  input  [31:0] A,
  input  [31:0] B,
  output [31:0] OUT,
  output ZERO
);

  wire [31:0] add_1_s, and_1_out, or_1_out, sub_1_s;

  assign or_1_out = B | A;  // Or or_1, 32 bits wide
  assign and_1_out = B & A;  // And and_1, 32 bits wide
  Add #(.Bits(32)) add_1 (.a(A), .b(B), .c_i(1'b0), .s(add_1_s));  // open: c_o
  Sub #(.Bits(32)) sub_1 (.a(A), .b(B), .c_i(1'b0), .s(sub_1_s));  // open: c_o
  Multiplexer #(.Selector_Bits(3), .Bits(32)) multiplexer_1 (
    .sel(ALU_CTR), .in_0(and_1_out), .in_1(or_1_out), .in_2(add_1_s), .in_3({32{1'b0}}), .in_4({32{1'b0}}),
    .in_5({32{1'b0}}), .in_6(sub_1_s), .in_7({32{1'b0}}), .out(OUT));
  Comparator #(.Bits(32)) comparator_1 (.a(OUT), .b({32{1'b0}}), .eq(ZERO));  // open: gt, lt
endmodule
