// Digital circuit Extender.dig as structural Verilog
module Extender (
  input  [15:0] imm16,
  input  Ext_Op,
  output [31:0] Ext_OUT
);

  wire [31:0] bitextender_1_out;

  BitExtender #(.inputBits(16), .outputBits(32)) bitextender_1 (.in(imm16), .out(bitextender_1_out));
  Multiplexer #(.Bits(32)) multiplexer_1 (
    .sel(Ext_Op), .in_0({{16{1'b0}}, imm16}), .in_1(bitextender_1_out), .out(Ext_OUT));
  // Pins of 1 and 16 bits meet at imm16
  // Pins of 1 and 32 bits meet at Ext_OUT
endmodule
