// Digital circuit instruction_memory.dig as structural Verilog
module instruction_memory (
  input  CLK,
  input  [23:0] A,
  output [31:0] D,
  output [5:0] OP,
  output [4:0] Rt,
  output [4:0] Rs,
  output [4:0] Rd,
  output [4:0] Shamt,
  output [5:0] Func,
  output [15:0] imm16
);

  wire demultiplexer_1_out_0, demultiplexer_1_out_1, demultiplexer_1_out_2, demultiplexer_1_out_3,
       pulldown_1_out, pulldown_2_out, pullup_1_out, pullup_2_out, pullup_3_out;
  wire [1:0] SEL;
  wire [7:0] rom_1_d;
  wire [23:0] add_1_s;

  PullDown pulldown_1 (.out(pulldown_1_out));
  PullUp pullup_1 (.out(pullup_1_out));
  PullDown pulldown_2 (.out(pulldown_2_out));
  Add #(.Bits(24)) add_1 (.a(A), .b({{22{1'b0}}, SEL}), .c_i(pulldown_1_out), .s(add_1_s));  // open: c_o
  Counter #(.Bits(2)) counter_1 (.en(pullup_1_out), .C(CLK), .clr(pulldown_2_out), .out(SEL));  // open: ovf
  PullUp pullup_2 (.out(pullup_2_out));
  ROM #(.AddrBits(24), .Bits(8)) rom_1 (.A(add_1_s), .sel(pullup_2_out), .D(rom_1_d));
  Register #(.Bits(8)) register_1 (.D(rom_1_d), .C(CLK), .en(demultiplexer_1_out_3), .Q(D[31:24]));
  Register #(.Bits(8)) register_2 (.D(rom_1_d), .C(CLK), .en(demultiplexer_1_out_2), .Q(D[23:16]));
  PullUp pullup_3 (.out(pullup_3_out));
  Demultiplexer #(.Selector_Bits(2)) demultiplexer_1 (
    .sel(SEL), .in(pullup_3_out), .out_0(demultiplexer_1_out_0), .out_1(demultiplexer_1_out_1),
    .out_2(demultiplexer_1_out_2), .out_3(demultiplexer_1_out_3));
  Register #(.Bits(8)) register_3 (.D(rom_1_d), .C(CLK), .en(demultiplexer_1_out_1), .Q(D[15:8]));
  Register #(.Bits(8)) register_4 (.D(rom_1_d), .C(CLK), .en(demultiplexer_1_out_0), .Q(D[7:0]));

  assign Func = D[5:0];
  assign imm16 = D[15:0];
  assign OP = D[31:26];
  assign Rd = D[15:11];
  assign Rs = D[25:21];
  assign Rt = D[20:16];
  assign Shamt = D[10:6];

  // Notes on the sheet:
  //   CLK: Hz: 2147483647
  //   contents of rom_1 (hex, n*v repeats v):
  //   fd,0,13,20,15,0,13,ac,15,0,14,8c,4*0,11,0,1,20,b,0,2,20,20,18
  //   ,22,0,22,20,22,0,25,28,22,0,24,30,22,0,0,0,9,20,5,0,a,20,f7,ff
  //   ,49,11,1,0,29,21,fd,ff,0,8
endmodule
